// Logisim project p1.circ as structural Verilog: 2 circuits, main circuit main
module main (
  input  A,
  input  B,
  input  C,
  input  D,
  output V,
  output W,
  output X,
  output y,
  output z
);

  wire and_1_out, and_2_out, and_3_out, and_4_out, and_5_out, and_6_out, not_1_out, not_2_out, not_3_out,
       or_1_out, xor_1_out;

  not not_1 (not_1_out, A);
  not not_2 (not_2_out, B);
  not not_3 (not_3_out, D);
  and and_1 (and_1_out, C, D);
  and and_2 (and_2_out, A, not_3_out);
  or or_1 (or_1_out, C, D);
  and and_3 (and_3_out, not_1_out, not_2_out);
  or or_2 (X, B, and_1_out);
  or or_3 (y, B, and_2_out);
  and and_4 (and_4_out, B, or_1_out);
  xor xor_1 (xor_1_out, B, C);
  and and_5 (and_5_out, D, and_3_out);
  and and_6 (and_6_out, C, not_3_out);
  or or_4 (z, A, and_4_out);
  or or_5 (V, xor_1_out, and_5_out);
  or or_6 (W, xor_1_out, and_6_out);

  // Notes on the sheet:
  //   !D
  //   !C
  //   C
  //   D
  //   !B
  //   B
  //   !A
  //   A
  //   binary to morse
  //   1 - led off | 2 - led on
  //   C⋅D+B
  //   B+A⋅~D
  //   B⋅D+B⋅C+A
  //   ~B⋅C+B⋅~C+~B⋅D
  //   ~B⋅C+B⋅~C+C⋅~D
endmodule

module nandSoln (
  input  A,
  input  B,
  input  C,
  input  D,
  output V,
  output W,
  output X,
  output y,
  output z
);

  wire nand_1_out, nand_2_out, nand_3_out, nand_4_out, nand_5_out, nand_6_out, nand_7_out, nand_8_out,
       nand_9_out, nand_10_out, nand_11_out, nand_12_out, nand_13_out, nand_14_out, nand_15_out, nand_16_out,
       nand_17_out, nand_18_out, nand_19_out, nand_20_out, nand_21_out, nand_22_out, nand_23_out,
       nand_25_out, nand_26_out, nand_28_out, nand_29_out, nand_30_out, nand_31_out, nand_32_out,
       nand_33_out, nand_34_out, nand_38_out, undriven, undriven_2;

  nand nand_1 (nand_1_out, A, A);
  nand nand_2 (nand_2_out, B, B);
  nand nand_3 (nand_3_out, D, D);
  nand nand_4 (nand_4_out, nand_1_out, nand_2_out);
  nand nand_5 (nand_5_out, C, D);
  nand nand_6 (nand_6_out, A, nand_3_out);
  nand nand_7 (nand_7_out, nand_4_out, nand_4_out);
  nand nand_8 (nand_8_out, C, nand_3_out);
  nand nand_9 (nand_9_out, nand_5_out, nand_5_out);
  nand nand_10 (nand_10_out, nand_6_out, nand_6_out);
  nand nand_11 (nand_11_out, C, C);
  nand nand_12 (nand_12_out, D, D);
  nand nand_13 (nand_13_out, B, C);
  nand nand_14 (nand_14_out, D, nand_7_out);
  nand nand_15 (nand_15_out, nand_8_out, nand_8_out);
  nand nand_16 (nand_16_out, B, B);
  nand nand_17 (nand_17_out, nand_9_out, nand_9_out);
  nand nand_18 (nand_18_out, B, B);
  nand nand_19 (nand_19_out, nand_10_out, nand_10_out);
  nand nand_20 (nand_20_out, nand_11_out, nand_12_out);
  nand nand_21 (nand_21_out, B, nand_13_out);
  nand nand_22 (nand_22_out, nand_13_out, C);
  nand nand_23 (nand_23_out, nand_14_out, nand_14_out);
  nand nand_24 (X, nand_16_out, nand_17_out);
  nand nand_25 (nand_25_out, B, nand_20_out);
  nand nand_26 (nand_26_out, nand_21_out, nand_22_out);
  nand nand_27 (y, nand_18_out, nand_19_out);
  nand nand_28 (nand_28_out, nand_25_out, nand_25_out);
  nand nand_29 (nand_29_out, nand_26_out, nand_26_out);
  nand nand_30 (nand_30_out, nand_23_out, nand_23_out);
  nand nand_31 (nand_31_out, nand_26_out, nand_26_out);
  nand nand_32 (nand_32_out, nand_15_out, nand_15_out);
  nand nand_33 (nand_33_out, A, A);
  nand nand_34 (nand_34_out, nand_28_out, nand_28_out);
  nand nand_35 (W, nand_31_out, nand_32_out);
  nand nand_36 (z, nand_33_out, nand_34_out);
  nand nand_37 (V, nand_29_out, nand_30_out);
  // AND_Gate and_1 is placed but not wired
  // OR_Gate or_1 is placed but not wired
  // XOR_Gate xor_1 is placed but not wired
  nand nand_38 (nand_38_out, undriven, undriven_2);
  // NAND_Gate nand_39 has open pins: in0=nand_38_out, in1=nand_38_out, out=open

  // Notes on the sheet:
  //   !D
  //   !C
  //   C
  //   D
  //   binary to morse
  //   1 - led off | 2 - led on
  //   !B
  //   B
  //   !A
  //   A
  //   xor
  //   B⋅D+B⋅C+A
  //   ~B⋅C+B⋅~C+C⋅~D
  //   C⋅D+B
  //   B+A⋅~D
  //   ~B⋅C+B⋅~C+~B⋅D
endmodule
